# Fritzing sketch simple-jack (saved by Fritzing 0.9.3b)
breadboards: 1

parts:
  Part1 = Arduino Uno (Rev3)
  S1 = Pushbutton [package="[THT]"]
  Part2 = Arduino Uno (Rev3)
  LED1 = LED - 5mm [color="Red (633nm)" package="5 mm [THT]"]
  R1 = Resistor [tolerance=±5% resistance=220 package=THT]
  Power_plug1 = Power plug
  Power_plug2 = Power plug

nets:
  N1: Part1.D11_PWM/MOSI, S1.Pin_3, S1.Pin_4
  N2: Part1.D12/MISO, Part2.D11_PWM/MOSI
  VIN: Part1.VIN, Power_plug2.VCC
  GND: S1.Pin_1, S1.Pin_2, LED1.cathode, Power_plug1.GND, Power_plug2.GND
  N3: Part2.D12/MISO, R1.Pin_1
  VIN_2: Part2.VIN, Power_plug1.VCC
  N4: LED1.anode, R1.Pin_0
